# Fritzing sketch CCS811 (saved by Fritzing 0.9.3b)
breadboards: 1

parts:
  U2 = NodeMCU V1.0
  Part3 = Adafruit CCS811

nets:
  N1: U2.D1, Part3.SCL
  N2: U2.D2, Part3.SDA
  3V3: U2.3V3, Part3.VIN
  GND: U2.GND, Part3.GND, Part3.!WAKE

custom parts:
  NodeMCU V1.0: ESP8266 based NodeMCU
